# Fritzing sketch прототип 1 закревский (saved by Fritzing 0.9.3b)
breadboards: 1

parts:
  Часть1 = Arduino Uno (Rev3)
  J1 = Piezo Speaker
  Display1 = 4-Digit 7-segment LED Display [package=THT]
  S1 = Toggle Switch [package=THT]
  VCC1 = Battery
  Q1 = PNP-Transistor [package="TO92 [THT]"]

nets:
  N1: Часть1.D2, Q1.B
  N2: Часть1.D3_PWM, Display1.DIO
  N3: Часть1.D4, Display1.VCC
  GND: Часть1.GND, J1.pin1, Display1.GND, S1.L2
  N4: Часть1.VIN, Display1.CLK, VCC1.+, Q1.C
  N5: S1.L1, VCC1.-

custom parts:
  4-Digit 7-segment LED Display: A 4-digit 7-segments LED display PCB module driven by a TM1637 control IC via 1-wire protocol.
